# Fritzing sketch arduino_mini_pro (saved by Fritzing 0.9.3b)
circuit board: 6.84986cm x 4.61896cm
breadboards: 1

parts:
  arduino_pro_mini = Arduino Pro Mini (3.3V)
  TA7791P = TA7291P [package=HSIP10-P-2.54(THT)]
  TA7791P_2 = TA7291P [package=HSIP10-P-2.54(THT)]
  M1 = DC Motor
  M2 = DC Motor
  LED1 = LED - 5mm [color="Red (633nm)" package="5 mm [THT]"]
  R1 = Resistor [tolerance=±5% resistance=1k package=THT]
  R2 = Resistor [tolerance=±5% resistance=1k package=THT]
  R3 = Resistor [tolerance=±5% resistance=1k package=THT]
  LED2 = LED - 5mm [color="Red (633nm)" package="5 mm [THT]"]
  R4-opt = Photocell (LDR) [package=THT]
  VCC1 = Battery
  R5 = Resistor [tolerance=±5% resistance=0 package=THT]
  DC-IN(5_25V) = Resistor [tolerance=±5% resistance=0 package=THT]
  DC-OUT(5V) = Resistor [tolerance=±5% resistance=0 package=THT]

nets:
  GND: arduino_pro_mini.GND, TA7791P.GND, TA7791P_2.GND, LED1.cathode, LED2.cathode, R4-opt.pin_1, VCC1.-, DC-IN(5_25V).Pin_1, DC-OUT(5V).Pin_1
  N1: arduino_pro_mini.RAW, DC-OUT(5V).Pin_0
  N2: arduino_pro_mini.VCC, R1.Pin_0
  N3: arduino_pro_mini.A2, R2.Pin_0
  N4: arduino_pro_mini.A1, R3.Pin_0
  N5: arduino_pro_mini.A0, R1.Pin_1, R4-opt.pin_0
  N6: arduino_pro_mini.D7, TA7791P.IN2
  N7: arduino_pro_mini.D6, TA7791P.Vref
  N8: arduino_pro_mini.D5, TA7791P.IN1
  N9: arduino_pro_mini.D4, TA7791P_2.IN2
  N10: arduino_pro_mini.D3, TA7791P_2.Vref
  N11: arduino_pro_mini.D2, TA7791P_2.IN1
  N12: TA7791P.OUT1, M1.pin_2
  VCC: TA7791P.Vcc, TA7791P.Vs, TA7791P_2.Vcc, TA7791P_2.Vs, R5.Pin_0
  N13: TA7791P.OUT2, M1.pin_1
  N14: TA7791P_2.OUT1, M2.pin_2
  N15: TA7791P_2.OUT2, M2.pin_1
  N16: LED1.anode, R2.Pin_1
  N17: R3.Pin_1, LED2.anode
  N18: VCC1.+, R5.Pin_1, DC-IN(5_25V).Pin_0

notes:
  igapon@gmail.com

custom parts:
  TA7291P: The IC are Full-Bridge Driver. 4 modes available (CW / CCW / STOP / BRAKE) and PWM control. Output current:1.0 A (AVE.) 2.0 A (PEAK)
