# Fritzing sketch 回路図arduino_mini_pro (saved by Fritzing 0.9.3b)
breadboards: 1

parts:
  パーツ1 = Arduino Pro Mini (3.3V)
  U1 = TA7291P [package=HSIP10-P-2.54(THT)]
  U2 = TA7291P [package=HSIP10-P-2.54(THT)]
  M1 = DC Motor
  M2 = DC Motor
  LED1 = LED - 5mm [color="Red (633nm)" package="5 mm [THT]"]
  R1 = Resistor [tolerance=±5% resistance=1k package=THT]
  R2 = Resistor [tolerance=±5% resistance=1k package=THT]
  R3 = Resistor [tolerance=±5% resistance=1k package=THT]
  LED2 = LED - 5mm [color="Red (633nm)" package="5 mm [THT]"]
  R4 = Photocell (LDR) [package=THT]
  VCC1 = Battery
  VCC2 = Battery
  IC1 = IC, DIP package, 34 pins [chip_label=IC]
  IC2 = IC, DIP package, 34 pins [chip_label=IC]

nets:
  N1: パーツ1.RAW, IC2.pin17, IC2.pin18
  GND: パーツ1.GND, U1.GND, U2.GND, LED1.cathode, LED2.cathode, R4.pin_1, VCC2.-, IC1.pin1, IC1.pin17, IC1.pin18, IC1.pin34
  VCC: パーツ1.VCC, U1.Vcc, U2.Vcc, R1.Pin_0
  N2: パーツ1.A2, R2.Pin_0
  N3: パーツ1.A1, R3.Pin_0
  N4: パーツ1.A0, R1.Pin_1, R4.pin_0
  N5: パーツ1.D7, U1.IN2
  N6: パーツ1.D6, U1.Vref
  N7: パーツ1.D5, U1.IN1
  N8: パーツ1.D4, U2.IN2
  N9: パーツ1.D3, U2.Vref
  N10: パーツ1.D2, U2.IN1
  N11: U1.OUT1, M1.pin_2
  N12: U1.Vs, U2.Vs, VCC1.+, IC2.pin1, IC2.pin34
  N13: U1.OUT2, M1.pin_1
  N14: U2.OUT1, M2.pin_2
  N15: U2.OUT2, M2.pin_1
  N16: LED1.anode, R2.Pin_1
  N17: R3.Pin_1, LED2.anode
  N18: VCC1.-, VCC2.+
  N19: IC1.pin2, IC1.pin33
  N20: IC1.pin3, IC1.pin32
  N21: IC1.pin4, IC1.pin31
  N22: IC1.pin5, IC1.pin30
  N23: IC1.pin6, IC1.pin29
  N24: IC1.pin7, IC1.pin28
  N25: IC1.pin8, IC1.pin27
  N26: IC1.pin9, IC1.pin26
  N27: IC1.pin10, IC1.pin25
  N28: IC1.pin11, IC1.pin24
  N29: IC1.pin12, IC1.pin23
  N30: IC1.pin13, IC1.pin22
  N31: IC1.pin14, IC1.pin21
  N32: IC1.pin15, IC1.pin20
  N33: IC1.pin16, IC1.pin19
  N34: IC2.pin2, IC2.pin33
  N35: IC2.pin3, IC2.pin32
  N36: IC2.pin4, IC2.pin31
  N37: IC2.pin5, IC2.pin30
  N38: IC2.pin6, IC2.pin29
  N39: IC2.pin7, IC2.pin28
  N40: IC2.pin8, IC2.pin27
  N41: IC2.pin9, IC2.pin26
  N42: IC2.pin10, IC2.pin25
  N43: IC2.pin11, IC2.pin24
  N44: IC2.pin12, IC2.pin23
  N45: IC2.pin13, IC2.pin22
  N46: IC2.pin14, IC2.pin21
  N47: IC2.pin15, IC2.pin20
  N48: IC2.pin16, IC2.pin19

custom parts:
  TA7291P: The IC are Full-Bridge Driver. 4 modes available (CW / CCW / STOP / BRAKE) and PWM control. Output current:1.0 A (AVE.) 2.0 A (PEAK)
