# Fritzing sketch 回路図arduino_uno (saved by Fritzing 0.9.3b)
circuit board: 5.33154cm x 5.16346cm
breadboards: 1

parts:
  U2 = TA7291P [package=HSIP10-P-2.54(THT)]
  M1 = DC Motor
  M2 = DC Motor
  LED1 = LED - 5mm [color="Red (633nm)" package="5 mm [THT]"]
  R1 = Resistor [tolerance=±5% resistance=1k package=THT]
  R2 = Resistor [tolerance=±5% resistance=1k package=THT]
  R3 = Resistor [tolerance=±5% resistance=1k package=THT]
  LED2 = LED - 5mm [color="Red (633nm)" package="5 mm [THT]"]
  R4 = Photocell (LDR) [package=THT]
  VCC2 = Battery block 9V
  パーツ1 = Arduino Uno (Rev3)
  U1 = TA7291P [package=HSIP10-P-2.54(THT)]

nets:
  GND: U2.GND, LED1.cathode, LED2.cathode, R4.pin_1, VCC2.-, パーツ1.GND, U1.GND
  N1: U2.OUT1, M2.pin_2
  N2: U2.Vref, パーツ1.D3_PWM
  N3: U2.IN1, パーツ1.D2
  N4: U2.IN2, パーツ1.D4
  VCC: U2.Vcc, R1.Pin_0, パーツ1.5V, U1.Vcc
  N5: U2.Vs, VCC2.+, パーツ1.VIN, U1.Vs
  N6: U2.OUT2, M2.pin_1
  N7: M1.pin_1, U1.OUT2
  N8: M1.pin_2, U1.OUT1
  N9: LED1.anode, R2.Pin_1
  N10: R1.Pin_1, R4.pin_0, パーツ1.A0
  N11: R2.Pin_0, パーツ1.A2
  N12: R3.Pin_0, LED2.anode
  N13: R3.Pin_1, パーツ1.A1
  N14: パーツ1.D5_PWM, U1.IN1
  N15: パーツ1.D6_PWM, U1.Vref
  N16: パーツ1.D7, U1.IN2

custom parts:
  TA7291P: The IC are Full-Bridge Driver. 4 modes available (CW / CCW / STOP / BRAKE) and PWM control. Output current:1.0 A (AVE.) 2.0 A (PEAK)
